# Fritzing sketch Scanduino Fritzing diagram (saved by Fritzing 0.7.11b)
breadboards: 1

parts:
  Arduino1 = Arduino
  U1 = Optocoupler [package=THT]
  U2 = Optocoupler [package=THT]
  M1 = Stepper Motor - Bipolar
  S1 = Pushbutton [package="[THT]"]
  Part1 = EasyDriver_v44
  R7 = Resistor [tolerance=±5% resistance=330 package=THT]
  R8 = Resistor [tolerance=±5% resistance=330 package=THT]
  Part2 = DeuLigne 1.1 - The Snootlab's LCD shield for Arduino
  S5 = Pushbutton [package="[THT]"]
  S6 = Pushbutton [package="[THT]"]
  S7 = Pushbutton [package="[THT]"]
  S8 = Pushbutton [package="[THT]"]
  Part3 = EasyDriver_v44
  M2 = Stepper Motor - Bipolar
  ENCODER1 = Rotary Encoder with Knob
  Part4 = Thumb Joystick
  TRS1 = Audio Jack (TRS) 3.5mm [package="PG203J [THT]"]

nets:
  N1: Arduino1.D12, Part4.SEL
  N2: Arduino1.D11, R8.Pin_1
  N3: Arduino1.D10, R7.Pin_1
  N4: Arduino1.D9, S7.Pin_3
  N5: Arduino1.D8, S6.Pin_1
  N6: Arduino1.D7, Part3.STEP
  N7: Arduino1.D6, Part3.DIR
  N8: Arduino1.D5, Part1.STEP
  N9: Arduino1.D4, Part1.DIR
  N10: Arduino1.D3, ENCODER1.no_name_yet#4
  N11: Arduino1.D2, S1.Pin_3, S1.Pin_4
  +5V: Arduino1.+5V, Part2.+5V, Part4.VCC
  GND: Arduino1.GND, U1.Pin_2, U1.Pin_4, U2.Pin_2, U2.Pin_4, S1.Pin_1, S1.Pin_2, Part1.GND, Part2.GND, S7.Pin_1, S7.Pin_2, S8.Pin_3, S8.Pin_4, Part3.GND, ENCODER1.no_name_yet#2, ENCODER1.no_name_yet#5, Part4.GND, TRS1.Sleeve
  N12: Arduino1.A0, ENCODER1.no_name_yet#3
  N13: Arduino1.A1, ENCODER1.no_name_yet#1
  N14: Arduino1.A2, Part4.HORZ
  N15: Arduino1.A3, Part4.VERT
  N16: Arduino1.A4, Part2.A4(SDA)
  N17: Arduino1.A5, Part2.A5(CLK)
  N18: U1.Pin_1, R7.Pin_0
  N19: U1.Pin_5, TRS1.Ring
  N20: U2.Pin_1, R8.Pin_0
  N21: U2.Pin_5, TRS1.Tip
  N22: M1.A, Part1.OUT2A
  N23: M1.C, Part1.OUT2B
  N24: M1.B, Part1.OUT1A
  N25: M1.D, Part1.OUT1B
  N26: Part1.V+, Part3.V+
  N27: S5.Pin_2, S6.Pin_4
  N28: Part3.OUT2A, M2.A
  N29: Part3.OUT2B, M2.C
  N30: Part3.OUT1A, M2.B
  N31: Part3.OUT1B, M2.D

notes:
  limit X
  limit Y
  12V DC Power supply to Easydrivers
  3.5 jack to camera

custom parts:
  Rotary Encoder with Knob: Rotary Encoder with 1/4" Shaft and Knob
